// Logisim project OneBit.circ as structural Verilog: 16 circuits, main circuit main
module main (
  input  _2,
  input  _1,
  input  _0,
  input  Data,
  input  Reset,
  input  Clock
);

  wire A_2_data, A_2_write_data, aluopt_1_p, aluopt_1_s, aluopt_1_write_data, B, B_2_data, B_2_write_data,
       C_data, C_write_data, Cell_0_data, Cell_0_write_data, Cell_1_data, Cell_1_write_data,
       decodeunit_1_a_read_enable, decodeunit_1_ab_write_enable, decodeunit_1_alu_s_p,
       decodeunit_1_alu_write_enable, decodeunit_1_b_read_enable, decodeunit_1_bus_data,
       decodeunit_1_c_read_enable, decodeunit_1_c_write_enable, decodeunit_1_ram_address,
       decodeunit_1_ram_read_enable, decodeunit_1_ram_write_enable, ram_1_re_0, ram_1_re_1, ram_1_we_0,
       ram_1_we_1;

  DecodeUnit decodeunit_1 (
    .Data(Data), ._2(_2), ._1(_1), ._0(_0), .A_Read_Enable(decodeunit_1_a_read_enable),
    .B_Read_Enable(decodeunit_1_b_read_enable), .AB_Write_Enable(decodeunit_1_ab_write_enable),
    .C_Read_Enable(decodeunit_1_c_read_enable), .C_Write_Enable(decodeunit_1_c_write_enable),
    .Alu_Write_Enable(decodeunit_1_alu_write_enable), .Alu_S_P(decodeunit_1_alu_s_p),
    .Ram_Read_Enable(decodeunit_1_ram_read_enable), .Ram_Write_Enable(decodeunit_1_ram_write_enable),
    .Ram_Address(decodeunit_1_ram_address), .Bus_Data(decodeunit_1_bus_data));
  Ram ram_1 (
    .Read_Enable(decodeunit_1_ram_read_enable), .Write_Enable(decodeunit_1_ram_write_enable),
    .Address(decodeunit_1_ram_address), .RE_0(ram_1_re_0), .WE_0(ram_1_we_0), .RE_1(ram_1_re_1),
    .WE_1(ram_1_we_1));
  Register Cell_0 (
    .Clock(Clock), .Read_Enable(ram_1_re_0), .Read_Data(B), .Write_Enable(ram_1_we_0),
    .Write_Data(Cell_0_write_data), .Reset(Reset), .Data(Cell_0_data));
  Register Cell_1 (
    .Clock(Clock), .Read_Enable(ram_1_re_1), .Read_Data(B), .Write_Enable(ram_1_we_1),
    .Write_Data(Cell_1_write_data), .Reset(Reset), .Data(Cell_1_data));
  Bus bus_1 (
    .Bus_Input(Cell_1_write_data), .Bus_Input_2(Cell_0_write_data), .Bus_Input_3(decodeunit_1_bus_data),
    .Bus_Input_4(aluopt_1_write_data), .Bus_Input_5(C_write_data), .Bus_Output(B));
  AluOpt aluopt_1 (
    .A(A_2_write_data), .B(B_2_write_data), .Write_Enable(decodeunit_1_alu_write_enable),
    .Write_Data(aluopt_1_write_data), .S_P(decodeunit_1_alu_s_p), .S(aluopt_1_s), .P(aluopt_1_p));
  // Probe on ram_1_re_0
  // Probe on B
  // Probe on ram_1_we_0
  // Probe on Cell_0_write_data
  // Probe on Cell_0_data
  // Probe on ram_1_re_1
  // Probe on B
  // Probe on ram_1_we_1
  // Probe on Cell_1_write_data
  // Probe on Cell_1_data
  // Probe on B
  // Probe on A_2_write_data
  // Probe on B_2_write_data
  // Probe on aluopt_1_s
  // Probe on aluopt_1_p
  // Probe on decodeunit_1_alu_s_p
  // Probe on decodeunit_1_alu_write_enable
  // Probe on aluopt_1_write_data
  Register A_2 (
    .Clock(Clock), .Read_Enable(decodeunit_1_a_read_enable), .Read_Data(B),
    .Write_Enable(decodeunit_1_ab_write_enable), .Write_Data(A_2_write_data), .Reset(Reset), .Data(A_2_data));
  Register B_2 (
    .Clock(Clock), .Read_Enable(decodeunit_1_b_read_enable), .Read_Data(B),
    .Write_Enable(decodeunit_1_ab_write_enable), .Write_Data(B_2_write_data), .Reset(Reset), .Data(B_2_data));
  Register C (
    .Clock(Clock), .Read_Enable(decodeunit_1_c_read_enable), .Read_Data(B),
    .Write_Enable(decodeunit_1_c_write_enable), .Write_Data(C_write_data), .Reset(Reset), .Data(C_data));
  // Probe on decodeunit_1_a_read_enable
  // Probe on B
  // Probe on decodeunit_1_ab_write_enable
  // Probe on A_2_write_data
  // Probe on A_2_data
  // Probe on decodeunit_1_b_read_enable
  // Probe on B
  // Probe on decodeunit_1_ab_write_enable
  // Probe on B_2_write_data
  // Probe on B_2_data
  // Probe on decodeunit_1_c_read_enable
  // Probe on B
  // Probe on decodeunit_1_c_write_enable
  // Probe on C_write_data
  // Probe on C_data

  // Other names for the same wires on the sheet: C = Clock; R = Reset

  // Notes on the sheet:
  //   [000] Nop
  //   [001] Rom->A (D : Data)
  //   [010] Rom->B (D : Data)
  //   [011] Rom->C (D : Data)
  //   [100] Add->C (D : S\P)
  //   [101] C->AB (D : A\B)
  //   [110] Ram->C (D : Address)
  //   [111] C->Ram (D : Address)
endmodule

module HS (
  input  A,
  input  B,
  output S,
  output P
);

  wire nand_1_out, nand_2_out, nand_3_out;

  nand nand_1 (nand_1_out, A, B);
  nand nand_2 (nand_2_out, A, nand_1_out);
  nand nand_3 (nand_3_out, nand_1_out, B);
  not not_1 (P, nand_1_out);
  nand nand_4 (S, nand_2_out, nand_3_out);
endmodule

// Mux
module Multiplexer_2_1 (
  input  _0,
  input  _1,
  input  Address,
  output Q
);

  wire nand_1_out, nand_2_out, not_1_out;

  not not_1 (not_1_out, Address);
  nand nand_1 (nand_1_out, _0, not_1_out);
  nand nand_2 (nand_2_out, _1, Address);
  nand nand_3 (Q, nand_1_out, nand_2_out);
endmodule

module Decoder_3_8 (
  input  _0,
  input  _1,
  input  _2,
  output _0_2,
  output _1_2,
  output _2_2,
  output _3,
  output _4,
  output _5,
  output _6,
  output _7
);

  wire not_1_out, not_2_out, not_3_out;

  not not_1 (not_1_out, _0);
  not not_2 (not_2_out, _1);
  not not_3 (not_3_out, _2);
  nand nand_1 (_0_2, not_1_out, not_2_out, not_3_out);
  nand nand_2 (_1_2, _0, not_2_out, not_3_out);
  nand nand_3 (_2_2, not_1_out, not_3_out, _1);
  nand nand_4 (_3, not_3_out, _0, _1);
  nand nand_5 (_4, not_1_out, not_2_out, _2);
  nand nand_6 (_5, not_2_out, _0, _2);
  nand nand_7 (_6, not_1_out, _1, _2);
  nand nand_8 (_7, _0, _1, _2);
endmodule

module D_Trigger (
  input  C,
  input  D,
  input  R,
  output Q,
  output NQ
);

  wire nand_1_out, nand_2_out, not_1_out, not_2_out;

  not not_1 (not_1_out, D);
  not not_2 (not_2_out, R);
  nand nand_1 (nand_1_out, D, C);
  nand nand_2 (nand_2_out, C, not_1_out);
  nand nand_3 (Q, nand_1_out, NQ);
  nand nand_4 (NQ, Q, nand_2_out, not_2_out);
endmodule

module Register (
  input  Clock,
  input  Read_Enable,
  input  Read_Data,
  input  Write_Enable,
  input  Reset,
  output Data,
  output Write_Data
);

  wire d_trigger_1_nq, nand_1_out, nor_1_out, not_1_out, not_2_out;

  not not_1 (not_1_out, Clock);
  not not_2 (not_2_out, Read_Enable);
  nor nor_1 (nor_1_out, not_1_out, not_2_out);
  nand nand_1 (nand_1_out, Data, Write_Enable);
  not not_3 (Write_Data, nand_1_out);
  D_Trigger d_trigger_1 (.C(nor_1_out), .D(Read_Data), .R(Reset), .Q(Data), .NQ(d_trigger_1_nq));

  // Notes on the sheet:
  //   Входы делаем с инверторов, потому что на них нужно вешать светодиоды
endmodule

module Ram (
  input  Read_Enable,
  input  Write_Enable,
  input  Address,
  output RE_0,
  output WE_0,
  output RE_1,
  output WE_1
);

  wire not_1_out, not_2_out, not_3_out;

  not not_1 (not_1_out, Read_Enable);
  not not_2 (not_2_out, Write_Enable);
  not not_3 (not_3_out, Address);
  nor nor_1 (RE_0, Address, not_1_out);
  nor nor_2 (RE_1, not_1_out, not_3_out);
  nor nor_3 (WE_0, Address, not_2_out);
  nor nor_4 (WE_1, not_2_out, not_3_out);
endmodule

module DecodeUnit (
  input  _2,
  input  _1,
  input  _0,
  input  Data,
  output A_Read_Enable,
  output B_Read_Enable,
  output AB_Write_Enable,
  output C_Read_Enable,
  output C_Write_Enable,
  output Alu_Write_Enable,
  output Alu_S_P,
  output Ram_Read_Enable,
  output Ram_Write_Enable,
  output Ram_Address,
  output Bus_Data
);

  wire decoder_3_8_1__1_2, decoder_3_8_1__2_2, decoder_3_8_1__3, decoder_3_8_1__4, decoder_3_8_1__5,
       decoder_3_8_1__6, decoder_3_8_1__7, nand_1_out, nand_2_out, nor_1_out, not_1_out, not_2_out,
       not_3_out, not_5_out, not_8_out;

  Decoder_3_8 decoder_3_8_1 (
    ._0(_0), ._1(_1), ._2(_2), ._1_2(decoder_3_8_1__1_2), ._2_2(decoder_3_8_1__2_2), ._3(decoder_3_8_1__3),
    ._4(decoder_3_8_1__4), ._5(decoder_3_8_1__5), ._6(decoder_3_8_1__6), ._7(decoder_3_8_1__7));  // open: _0_2
  not not_1 (not_1_out, decoder_3_8_1__1_2);
  not not_2 (not_2_out, decoder_3_8_1__2_2);
  not not_3 (not_3_out, decoder_3_8_1__3);
  not not_4 (AB_Write_Enable, decoder_3_8_1__4);
  not not_5 (not_5_out, decoder_3_8_1__5);
  not not_6 (Ram_Write_Enable, decoder_3_8_1__6);
  not not_7 (Ram_Read_Enable, decoder_3_8_1__7);
  not not_8 (not_8_out, Data);
  nand nand_1 (nand_1_out, not_8_out, not_5_out);
  nand nand_2 (nand_2_out, not_5_out, Data);
  nor nor_1 (nor_1_out, not_1_out, not_2_out, not_3_out);
  nand nand_3 (A_Read_Enable, nand_1_out, decoder_3_8_1__1_2);
  nand nand_4 (B_Read_Enable, nand_2_out, decoder_3_8_1__2_2);
  nand nand_5 (C_Read_Enable, decoder_3_8_1__6, decoder_3_8_1__4, decoder_3_8_1__3);
  nand nand_6 (C_Write_Enable, decoder_3_8_1__7, decoder_3_8_1__5);
  nor nor_2 (Bus_Data, nor_1_out, not_8_out);

  assign Alu_S_P = Data;
  assign Alu_Write_Enable = AB_Write_Enable;
  assign Ram_Address = Data;

  // Notes on the sheet:
  //   N1     N2     N3     N4     N5     N6     N7
  //   1        2        3       4        5        6       7
  //   ND       D
  //   [000] Nop
  //   [001] Rom->A (Data)
  //   [010] Rom->B (Data) 
  //   [011] Rom->C (Data)
  //   [100] Add->C (S\P)
  //   [101] C->AB (A\B)
  //   [110] Ram->C (Address)
  //   [111] C->Ram (Address)
endmodule

// Alu
module ALU (
  input  A,
  input  B,
  input  Write_Enable,
  input  S_P,
  output S,
  output P,
  output Write_Data
);

  wire multiplexer_2_1_1_q, nand_1_out;

  not not_1 (Write_Data, nand_1_out);
  nand nand_1 (nand_1_out, multiplexer_2_1_1_q, Write_Enable);
  HS hs_1 (.A(A), .B(B), .S(S), .P(P));
  Multiplexer_2_1 multiplexer_2_1_1 (._0(S), ._1(P), .Address(S_P), .Q(multiplexer_2_1_1_q));
endmodule

module Bus (
  input  Bus_Input,
  input  Bus_Input_2,
  input  Bus_Input_3,
  input  Bus_Input_4,
  input  Bus_Input_5,
  output Bus_Output
);

  wire nor_1_out;

  nor nor_1 (nor_1_out, Bus_Input, Bus_Input_2, Bus_Input_3, Bus_Input_4, Bus_Input_5);
  not not_1 (Bus_Output, nor_1_out);
endmodule

// Alu
module AluOpt (
  input  A,
  input  B,
  input  Write_Enable,
  input  S_P,
  output S,
  output P,
  output Write_Data
);

  wire and_1_out, and_2_out, and_3_out, and_4_out, nand_1_out, nor_2_out, nor_3_out, not_1_out, not_4_out;

  nand nand_1 (nand_1_out, A, B);
  nor nor_1 (Write_Data, nor_3_out, not_1_out);
  not not_1 (not_1_out, Write_Enable);
  and and_1 (and_1_out, A, nand_1_out);
  and and_2 (and_2_out, nand_1_out, B);
  not not_2 (P, nand_1_out);
  nor nor_2 (nor_2_out, and_1_out, and_2_out);
  not not_3 (S, nor_2_out);
  not not_4 (not_4_out, S_P);
  and and_3 (and_3_out, S, not_4_out);
  and and_4 (and_4_out, S_P, P);
  nor nor_3 (nor_3_out, and_3_out, and_4_out);
endmodule

module D_Trigger_2 (
  input  C,
  input  D,
  input  R,
  output Q,
  output NQ
);

  wire nand_1_out, nand_2_out, nand_3_out, nand_4_out, nand_5_out, nand_7_out;

  nand nand_1 (nand_1_out, D, D);
  nand nand_2 (nand_2_out, R, R);
  nand nand_3 (nand_3_out, D, C);
  nand nand_4 (nand_4_out, C, nand_1_out);
  nand nand_5 (nand_5_out, nand_4_out, nand_2_out);
  nand nand_6 (Q, nand_3_out, NQ);
  nand nand_7 (nand_7_out, nand_5_out, nand_5_out);
  nand nand_8 (NQ, Q, nand_7_out);
endmodule

module Register2 (
  input  Clock,
  input  Read_Enable,
  input  Read_Data,
  input  Write_Enable,
  input  Reset,
  output Data,
  output Write_Data
);

  wire nand_1_out, nand_2_out, nand_3_out;

  nand nand_1 (nand_1_out, Clock, Read_Enable);
  nand nand_2 (nand_2_out, nand_1_out, nand_1_out);
  nand nand_3 (nand_3_out, Data, Write_Enable);
  nand nand_4 (Write_Data, nand_3_out, nand_3_out);
  D_Trigger_2 d_trigger_2_1 (.C(nand_2_out), .D(Read_Data), .R(Reset), .Q(Data));  // open: NQ
endmodule

module Ram2 (
  input  Read_Enable,
  input  Write_Enable,
  input  Address,
  output RE_0,
  output WE_0,
  output RE_1,
  output WE_1
);

  wire nand_1_out, nand_2_out, nand_3_out, nand_6_out, nand_7_out;

  nand nand_1 (nand_1_out, Address, Address);
  nand nand_2 (nand_2_out, nand_1_out, Read_Enable);
  nand nand_3 (nand_3_out, Read_Enable, Address);
  nand nand_4 (RE_0, nand_2_out, nand_2_out);
  nand nand_5 (RE_1, nand_3_out, nand_3_out);
  nand nand_6 (nand_6_out, nand_1_out, Write_Enable);
  nand nand_7 (nand_7_out, Write_Enable, Address);
  nand nand_8 (WE_0, nand_6_out, nand_6_out);
  nand nand_9 (WE_1, nand_7_out, nand_7_out);
endmodule

module Bus2 (
  input  Bus_Input,
  input  Bus_Input_2,
  input  Bus_Input_3,
  input  Bus_Input_4,
  input  Bus_Input_5,
  input  Bus_Input_6,
  input  Bus_Input_7,
  input  Bus_Input_8,
  input  Bus_Input_9,
  input  Bus_Input_10,
  input  Bus_Input_11,
  input  Bus_Input_12,
  output Bus_Output
);

  wire nand_1_out, nand_2_out, nand_3_out, nand_4_out, nand_5_out, not_1_out, not_2_out, not_3_out,
       not_4_out, not_5_out, not_6_out, not_7_out, not_8_out, not_9_out, not_10_out, or_1_out, or_2_out,
       or_3_out, or_4_out;

  or or_1 (or_1_out, Bus_Input_2, Bus_Input_3);
  or or_2 (or_2_out, Bus_Input_4, Bus_Input_5);
  not not_1 (not_1_out, Bus_Input_8);
  not not_2 (not_2_out, Bus_Input_9);
  not not_3 (not_3_out, Bus_Input_10);
  not not_4 (not_4_out, Bus_Input_11);
  or or_3 (or_3_out, Bus_Input, or_1_out);
  or or_4 (or_4_out, or_2_out, Bus_Input_6);
  not not_5 (not_5_out, Bus_Input_7);
  nand nand_1 (nand_1_out, not_1_out, not_2_out);
  not not_6 (not_6_out, nand_1_out);
  not not_7 (not_7_out, nand_2_out);
  nand nand_2 (nand_2_out, not_3_out, not_4_out);
  not not_8 (not_8_out, Bus_Input_12);
  nand nand_3 (nand_3_out, not_5_out, not_6_out);
  nand nand_4 (nand_4_out, not_7_out, not_8_out);
  or or_5 (Bus_Output, or_3_out, or_4_out);
  not not_9 (not_9_out, nand_3_out);
  not not_10 (not_10_out, nand_4_out);
  nand nand_5 (nand_5_out, not_9_out, not_10_out);
endmodule

module Register_3 (
  input  Clock,
  input  Read_Enable,
  input  Write_Enable,
  input  Read_Data_0,
  input  Read_Data_1,
  input  N_Reset,
  output Data_0,
  output N_Write_Data_0,
  output Data_1,
  output N_Write_Data_1
);

  wire nand_1_out, nand_2_out, nand_3_out, nand_4_out, nand_6_out, nand_8_out, nor_1_out, not_1_out,
       not_2_out, not_3_out, not_4_out;

  not not_1 (not_1_out, Clock);
  not not_2 (not_2_out, Read_Enable);
  nor nor_1 (nor_1_out, not_1_out, not_2_out);
  not not_3 (not_3_out, Read_Data_0);
  not not_4 (not_4_out, Read_Data_1);
  nand nand_1 (nand_1_out, Read_Data_0, nor_1_out);
  nand nand_2 (nand_2_out, nor_1_out, not_3_out);
  nand nand_3 (nand_3_out, Read_Data_1, nor_1_out);
  nand nand_4 (nand_4_out, nor_1_out, not_4_out);
  nand nand_5 (Data_0, nand_1_out, nand_6_out);
  nand nand_6 (nand_6_out, Data_0, nand_2_out, N_Reset);
  nand nand_7 (Data_1, nand_3_out, nand_8_out);
  nand nand_8 (nand_8_out, Data_1, nand_4_out, N_Reset);
  nand nand_9 (N_Write_Data_0, Data_0, Write_Enable);
  nand nand_10 (N_Write_Data_1, Data_1, Write_Enable);

  // Notes on the sheet:
  //   Инверторы для светодиодов
  //   Тут один транзистор для светодиода
endmodule
